// Logisim project Processor.circ as structural Verilog
// Pipeline
module PipeLine (
  input  Reset,
  input  [3:0] Display_Address,
  output [31:0] out_3
);

  wire alu_1_is, alu_1_is_2, BranchLock, checkstore_1_isstore, Clock_, control_unit_1_isimmediate,
       control_unit_1_isret, DataLock, EXRW_src1_out_4, EXRW_src2_out_4, flags_1_flags_e, flags_1_flags_gt,
       isRet_q, multiplexer_4_out, not_1_out, not_2_out, or_1_out, RW_EX_op2, RW_MA_op2;
  wire [1:0] F_M3, F_M4;
  wire [1:1] MA_src2_Conflict_out_4;
  wire [3:0] Control_2_q, Control_q, multiplexer_10_out, multiplexer_11_out, multiplexer_18_out;
  wire [6:0] control_unit_1_isubranch, data_2_q, multiplexer_19_out;
  wire [12:0] ALUsignals_q, control_unit_1_alusignals, multiplexer_14_out;
  wire [31:0] A_q, adder_1_out, adder_2_out, adder_3_out, alu_1_aluresult, aluResult_2_q, aluResult_4_q, B_q,
       bit_extender_1_out, Branch_Target_q, calculate_immediate_1_immx, EX, IF, ldResult_2_q, MA,
       memory_unit_1_ldresult, multiplexer_2_out, multiplexer_3_out, multiplexer_5_out, multiplexer_6_out,
       multiplexer_8_out, multiplexer_9_out, multiplexer_12_out, multiplexer_13_out, multiplexer_15_out,
       multiplexer_16_out, multiplexer_17_out, OF, op2_2_q, Op2_q, pC_3_q, pC_4_q, PC_5_q, PC_6_q, PC_q,
       register_file_1_displayd, register_file_1_readd1, register_file_1_readd2, RW, shifter_1_out;

  Clock Clock (.out(Clock_));
  DataLock datalock_1 (.Inst1(OF), .Inst2_Load(EX), .isDataLock(DataLock));
  Conflict_Src2 EXRW_src2 (.A(OF), .B(RW), .ra(4'b1111), .out_4(EXRW_src2_out_4));
  Conflict_Src1 EXRW_src1 (.A(OF), .B(RW), .ra(4'b1111), .out_4(EXRW_src1_out_4));
  Conflict_Src2 RW_src2_Conflict (.A(EX), .B(RW), .ra(4'b1111), .out_4(RW_EX_op2));
  Conflict_Src2 MA_src2_Conflict (.A(EX), .B(MA), .ra(4'b1111), .out_4(MA_src2_Conflict_out_4[1]));
  Conflict_Src1 RW_src1_conflict (.A(EX), .B(RW), .ra(4'b1111), .out_4(F_M3[0]));
  Conflict_Src1 MA_src1_conflict (.A(EX), .B(MA), .ra(4'b1111), .out_4(F_M3[1]));
  or or_1 (or_1_out, BranchLock, DataLock);
  checkStore checkstore_1 (.opcode(EX[31:27]), .isStore(checkstore_1_isstore));
  Multiplexer #(.width(2)) multiplexer_1 (
    .in0({MA_src2_Conflict_out_4[1], RW_EX_op2}), .in1(2'b00), .out(F_M4), .sel(checkstore_1_isstore));  // open: en
  Conflict_Src2 u_RW_MA_op2 (.A(MA), .B(RW), .ra(4'b1111), .out_4(RW_MA_op2));
  Multiplexer #(.width(32)) multiplexer_2 (
    .in0(OF), .in1(32'h68000000), .out(multiplexer_2_out), .sel(or_1_out));  // open: en
  Register #(.width(32)) PC (.D(PC_6_q), .Q(PC_q), .clk(Clock_));  // open: en, clr
  // Probe on pC_4_q
  // Probe on aluResult_4_q
  // Probe on ldResult_2_q
  not not_1 (not_1_out, DataLock);
  not not_2 (not_2_out, DataLock);
  Register #(.width(32)) Instruction (.D(multiplexer_2_out), .Q(EX), .clk(Clock_));  // open: en, clr
  Register #(.width(32)) pC_3 (.D(PC_q), .Q(pC_3_q), .clk(Clock_));  // open: en, clr
  Register #(.width(32)) pC_4 (.D(pC_3_q), .Q(pC_4_q), .clk(Clock_));  // open: en, clr
  Register #(.width(32)) PC_5 (.D(multiplexer_3_out), .en(not_1_out), .Q(PC_5_q), .clk(Clock_), .clr(Reset));
  assign bit_extender_1_out = {{5{OF[26]}}, OF[26:0]};  // Bit_Extender bit_extender_1
  Register #(.width(32)) Branch_Target (.D(adder_1_out), .Q(Branch_Target_q), .clk(Clock_));  // open: en, clr
  Register #(.width(32)) Instruction_2 (.D(EX), .Q(MA), .clk(Clock_));  // open: en, clr
  Register #(.width(32)) Instruction_3 (.D(MA), .Q(RW), .clk(Clock_));  // open: en, clr
  Multiplexer #(.width(32), .enable("false")) multiplexer_3 (
    .in0(adder_3_out), .in1(multiplexer_5_out), .out(multiplexer_3_out), .sel(BranchLock));
  Shifter #(.width(32)) shifter_1 (.in(bit_extender_1_out), .\dist (5'b00010), .out(shifter_1_out));
  Adder #(.width(32)) adder_1 (.a(shifter_1_out), .b(PC_6_q), .out(adder_1_out));  // open: cin, cout
  Multiplexer multiplexer_4 (
    .in0(control_unit_1_isret), .in1(1'b0), .out(multiplexer_4_out), .sel(or_1_out));  // open: en
  Register #(.width(1)) isRet (.D(multiplexer_4_out), .Q(isRet_q), .clk(Clock_));  // open: en, clr
  Multiplexer #(.width(32), .enable("false")) multiplexer_5 (
    .in0(Branch_Target_q), .in1(multiplexer_13_out), .out(multiplexer_5_out), .sel(isRet_q));
  ALU alu_1 (
    .A(multiplexer_13_out), .B(multiplexer_6_out), .ALUsignals(ALUsignals_q), .aluResult(alu_1_aluresult),
    .is(alu_1_is), .is_2(alu_1_is_2));
  Register #(.width(32)) aluResult_2 (.D(alu_1_aluresult), .Q(aluResult_2_q), .clk(Clock_));  // open: en, clr
  Adder #(.width(32)) adder_2 (.a(pC_4_q), .b(32'h4), .out(adder_2_out));  // open: cin, cout
  // Probe on out_3
  Adder #(.width(32)) adder_3 (.a(32'h4), .b(PC_5_q), .out(adder_3_out));  // open: cin, cout
  Register #(.width(32)) PC_6 (.D(PC_5_q), .en(not_2_out), .Q(PC_6_q), .clk(Clock_));  // open: clr
  Calculate_Immediate calculate_immediate_1 (.imm(OF[17:0]), .immx(calculate_immediate_1_immx));
  Register #(.width(32)) A (.D(multiplexer_12_out), .Q(A_q), .clk(Clock_));  // open: en, clr
  Multiplexer #(.select(2), .width(32)) multiplexer_6 (
    .in0(B_q), .in1(out_3), .in2(aluResult_2_q), .in3(aluResult_2_q), .out(multiplexer_6_out), .sel(F_M4));  // open: en
  // Probe on aluResult_2_q
  Register #(.width(32)) ldResult_2 (.D(memory_unit_1_ldresult), .Q(ldResult_2_q), .clk(Clock_));  // open: en, clr
  Multiplexer #(.select(2), .width(32), .enable("false")) multiplexer_7 (
    .in0(aluResult_4_q), .in1(ldResult_2_q), .in2(adder_2_out), .out(out_3),
    .sel({Control_2_q[0], Control_2_q[2]}));  // open: in3
  Multiplexer #(.width(32), .enable("false")) multiplexer_8 (
    .in0(register_file_1_readd2), .in1(out_3), .out(multiplexer_8_out), .sel(EXRW_src2_out_4));
  Multiplexer #(.width(32), .enable("false")) multiplexer_9 (
    .in0(multiplexer_8_out), .in1(calculate_immediate_1_immx), .out(multiplexer_9_out),
    .sel(control_unit_1_isimmediate));
  Register #(.width(32)) B (.D(multiplexer_9_out), .Q(B_q), .clk(Clock_));  // open: en, clr
  // Probe on A_q
  // Probe on B_q
  Flags flags_1 (
    .isCmp(ALUsignals_q[0]), .is(alu_1_is), .is_2(alu_1_is_2), .flags_GT(flags_1_flags_gt),
    .flags_E(flags_1_flags_e));
  Memory_Unit memory_unit_1 (
    .MAR(aluResult_2_q), .ldResult(memory_unit_1_ldresult), .MDR(multiplexer_17_out), .isSt(Control_q[1]),
    .isLd(Control_q[2]), .Clock(Clock_), .Reset(Reset));
  ROM #(.addrWidth(24), .dataWidth(32)) rom_1 (.addr(PC_5_q[25:2]), .data(IF));  // open: sel
  Multiplexer #(.width(4), .enable("false")) multiplexer_10 (
    .in0(OF[21:18]), .in1(4'b1111), .out(multiplexer_10_out), .sel(control_unit_1_isret));
  Multiplexer #(.width(4), .enable("false")) multiplexer_11 (
    .in0(OF[17:14]), .in1(OF[25:22]), .out(multiplexer_11_out), .sel(control_unit_1_isubranch[4]));
  Multiplexer #(.width(32), .enable("false")) multiplexer_12 (
    .in0(register_file_1_readd1), .in1(out_3), .out(multiplexer_12_out), .sel(EXRW_src1_out_4));
  Multiplexer #(.select(2), .width(32)) multiplexer_13 (
    .in0(A_q), .in1(out_3), .in2(aluResult_2_q), .in3(aluResult_2_q), .out(multiplexer_13_out), .sel(F_M3));  // open: en
  // Probe on multiplexer_17_out
  Register #(.width(32)) aluResult_4 (.D(aluResult_2_q), .Q(aluResult_4_q), .clk(Clock_));  // open: en, clr
  Register_File register_file_1 (
    .ReadA1(multiplexer_10_out), .ReadA2(multiplexer_11_out), .WriteE(Control_2_q[3]), .WriteD(out_3),
    .ReadD1(register_file_1_readd1), .ReadD2(register_file_1_readd2), .Clock(Clock_), .Reset(Reset),
    .DisplayD(register_file_1_displayd), .DisplayA(Display_Address), .WriteA(multiplexer_18_out));
  Multiplexer #(.width(13)) multiplexer_14 (
    .in0(control_unit_1_alusignals), .in1({13{1'b0}}), .out(multiplexer_14_out), .sel(or_1_out));  // open: en
  Register #(.width(32)) Op2 (.D(multiplexer_8_out), .Q(Op2_q), .clk(Clock_));  // open: en, clr
  Branch_Unit branch_unit_1 (
    .isBeq(data_2_q[2]), .isUBranch(data_2_q[0]), .flags_E(flags_1_flags_e), .isBgt(data_2_q[1]),
    .flags_GT(flags_1_flags_gt), .isBranchTaken(BranchLock));
  Multiplexer #(.width(32), .enable("false")) multiplexer_15 (
    .in0(IF), .in1(32'h68000000), .out(multiplexer_15_out), .sel(BranchLock));
  Control_Unit control_unit_1 (
    .isSt(control_unit_1_isubranch[4]), .isLd(control_unit_1_isubranch[5]),
    .isBeq(control_unit_1_isubranch[2]), .isBgt(control_unit_1_isubranch[1]), .isRet(control_unit_1_isret),
    .I_bit(OF[26]), .isImmediate(control_unit_1_isimmediate), .opcode(OF[31:27]),
    .isWb(control_unit_1_isubranch[6]), .isUbranch(control_unit_1_isubranch[0]),
    .isCall(control_unit_1_isubranch[3]), .ALUsignals(control_unit_1_alusignals));
  Register #(.width(13)) ALUsignals (.D(multiplexer_14_out), .Q(ALUsignals_q), .clk(Clock_));  // open: en, clr
  Multiplexer #(.width(32)) multiplexer_16 (
    .in0(Op2_q), .in1(out_3), .out(multiplexer_16_out), .sel(RW_EX_op2));  // open: en
  Multiplexer #(.width(32)) multiplexer_17 (
    .in0(op2_2_q), .in1(out_3), .out(multiplexer_17_out), .sel(RW_MA_op2));  // open: en
  Multiplexer #(.width(4), .enable("false")) multiplexer_18 (
    .in0(RW[25:22]), .in1(4'b1111), .out(multiplexer_18_out), .sel(Control_2_q[0]));
  Register #(.width(32)) Instruction_4 (.D(multiplexer_15_out), .en(not_2_out), .Q(OF), .clk(Clock_));  // open: clr
  Multiplexer #(.width(7)) multiplexer_19 (
    .in0(control_unit_1_isubranch), .in1({7{1'b0}}), .out(multiplexer_19_out), .sel(or_1_out));  // open: en
  Register #(.width(32)) op2_2 (.D(multiplexer_16_out), .Q(op2_2_q), .clk(Clock_));  // open: en, clr
  Register #(.width(7)) data_2 (.D(multiplexer_19_out), .Q(data_2_q), .clk(Clock_));  // open: en, clr
  Register #(.width(4)) Control (.D(data_2_q[6:3]), .Q(Control_q), .clk(Clock_));  // open: en, clr
  // Probe on register_file_1_displayd
  Register #(.width(4)) Control_2 (.D(Control_q), .Q(Control_2_q), .clk(Clock_));  // open: en, clr
  // Probe on IF
  // Probe on OF
  // Probe on MA
  // Probe on IF
  // Probe on OF
  // Probe on EX
  // Probe on MA
  // Probe on RW
  // Probe on out_3
  // Probe on EX
  // Probe on RW

  // Notes on the sheet:
  //   OF Stage
  //   EX Stage
  //   MA Stage
  //   RW Stage
  //   IF Stage
  //   IF-OF Register 
  //   OF-EX Registers
  //   EX-MA Registers
  //   MA-RW Registers
  //   pc
  //   branchTarget
  //   B
  //   pc
  //   imm
  //   offset
  //   isRet
  //   isRet
  //   A
  //   ALU
  //   aluResult
  //   MAR
  //   isBranchTaken
  //   pc+4
  //   branchTarget
  //   calc immx
  //   immx
  //   M4
  //   is>
  //   is=
  //   isCmp
  //   MDR
  //   Memory
  //   Unit
  //   ldResult
  //   data
  //   -------------------------------------------------------------------------------------------------------------------------------------------------------------------------------------------------------------------------------------------------------------------------------------------------------------------------------------------------------------------------------------
  //   -----------------------------------------------------------------------------------------------------------------------------------------------------------------------------------------------------------------------------------------------------------------------------------------------------------------------------------------------------------------------------------
  //   instruction
  //   rs2
  //   isSt
  //   M2
  //   isImmediate
  //   -----------------------------------------------------------------------------------------------------------------------------------------------------------------------------------------------------------------------------------------------------------------------------------------------------------------------------------------------------------------------------------------
  //   -------------------------------------------------------------------------------------------------------------------------------------------------------------------------------------------------------------------------------------------------------------------------------------------------------------------------------------------------------------------------------------------
  //   M3
  //   flags(GT)
  //   Flags
  //   flags(E)
  //   -------------------------------------------------------------------------------------------------------------------------------------------------------------------------------------------------------------------------------------------------------------------------------------------------------------------------------------------------------------------------------------------
  //   -------------------------------------------------------------------------------------------------------------------------------------------------------------------------------------------------------------------------------------------------------------------------------------------------------------------------------------------------------------------------------------------
  //   isLd
  //   isSt
  //   -------------------------------------------------------------------------------------------------------------------------------------------------------------------------------------------------------------------------------------------------------------------------------------------------------------------------------------------------------------------------------------------
  //   -------------------------------------------------------------------------------------------------------------------------------------------------------------------------------------------------------------------------------------------------------------------------------------------------------------------------------------------------------------------------------------------
  //   isLd
  //   isCall
  //   Pipelined Processor
  //   --------------------------------------------------------------------------------------------------------------------------------------------------------------------------------------------------------------------------------------------------------------------------------------------------------------------------------------------------------------------------------------------------------------------
  //   Instruction Memory
  //   contents of rom_1 (hex, n*v repeats v):
  //   4c000000 4c400031 7c400000 4c40003f 7c400004 4c400055 7c400008 4c400025 7c40000c 4c40005d 7c400010
  //   4c40003b 7c400014 4c40005f 7c400018 4c400064 7c40001c 4c40005a 7c400020 4c400038 7c400024 4c400047
  //   7c400028 4c40005d 7c40002c 4c400044 7c400030 4c400022 7c400034 4c400048 7c400038 4c400009 7c40003c
  //   4c400020 7c400040 4c400025 7c400044 4c400047 7c400048 4c400010 7c40004c 4c400021 7c400050 4c400059
  //   7c400054 4c400006 7c400058 4c400062 7c40005c 4c400045 7c400060 4c400008 7c400064 4c400003 7c400068
  //   4c400033 7c40006c 4c400063 7c400070 4c400043 7c400074 4c400016 7c400078 4c400053 7c40007c 4c40000b
  //   7c400080 4c400003 7c400084 4c400055 7c400088 4c40003f 7c40008c 4c40005a 7c400090 4c400013 7c400094
  //   4c40003f 7c400098 4c400024 7c40009c 4c400050 7c4000a0 4c400018 7c4000a4 4c400030 7c4000a8 4c400019
  //   7c4000ac 4c400030 7c4000b0 4c400023 7c4000b4 4c400024 7c4000b8 4c40001f 7c4000bc 4c400026 7c4000c0
  //   4c400038 7c4000c4 4c400006 7c4000c8 4c40001f 7c4000cc 4c40001c 7c4000d0 4c40005f 7c4000d4 4c400049
  //   7c4000d8 4c400041 7c4000dc 4c400008 7c4000e0 4c40004f 7c4000e4 4c40001d 7c4000e8 4c400019 7c4000ec
  //   4c400037 7c4000f0 4c400047 7c4000f4 4c400059 7c4000f8 4c400059 7c4000fc 4c40000d 7c400100 4c400043
  //   7c400104 4c40000c 7c400108 4c400009 7c40010c 4c400022 7c400110 4c400014 7c400114 4c400053 7c400118
  //   4c40004a 7c40011c 4c400036 7c400120 4c40003d 7c400124 4c400028 7c400128 4c400007 7c40012c 4c400013
  //   7c400130 4c400020 7c400134 4c400018 7c400138 4c400043 7c40013c 4c400048 7c400140 4c400021 7c400144
  //   4c400059 7c400148 4c400056 7c40014c 4c40004a 7c400150 4c40002d 7c400154 4c400059 7c400158 4c400050
  //   7c40015c 4c40003e 7c400160 4c400051 7c400164 4c40004a 7c400168 4c400012 7c40016c 4c40000c 7c400170
  //   4c40005c 7c400174 4c400030 7c400178 4c400031 7c40017c 4c400037 7c400180 4c40004e 7c400184 4c40003b
  //   7c400188 4c40000e 7c40018c 4c800000 4cc00005 14cc0004 108c000 4a438000 48008000 48410000 48c00000
  //   49004000 98000027 90000000 6640004 76180000 7e240000 5980004 28190000 88000044 97fffffa 6640004
  //   760c0000 7e240000 4cc0004 280d4000 8800003d 97fffffa 7ca40000 4cc0004 9000002d 75d40000 7e140000
  //   7dd80000 5540004 a0000000 49410000 280d0000 88000004 4cc0004 d100004 97fffffb a0000000 280d0000
  //   88000006 76240000 7e0c0000 4cc0004 6640004 97fffffa a0000000 280d0000 88000016 80000015 6640010
  //   7fe40000 7ce40004 7d24000c 9fffffea 7d640008 74e40004 49014000 9ffffff5 7524000c 75640008 4d40004
  //   9ffffff1 74e40004 75640008 7524000c 5940004 98000011 77e40000 e640010 a0000000 280d4000 8fffffc2
  //   28190000 8fffffc7 6640004 748c0000 76180000 28208000 8fffffc9 7e240000 5980004 97fffff5 a0000000
  //   6640010 49c24000 7fe40000 7ce40004 7d640008 7da4000c 7d240010 6640010 9fffffeb 4a41c000 74e40004
  //   75240010 65c0014 9fffffc6 4a41c000 77e40000 e640010 a0000000
  //   nop
  //   rs1
  //   rd
  //   Register
  //   File
  //   op1
  //   op2
  //   Branch
  //   Unit
  //   ------------------------------------------------------------------------------------------------------------------------------------------------------------------------------------------------------------------------------------------------------------------------------------------------------------------------------------------------------------------------------------------------------------------
  //   isRet
  //   isWb
  //   E
  //   address
  //   A
  //   data
  //   D
  //   M1
  //   isBranchTaken
  //   rd
  //   opcode
  //   I bit
  //   isWb
  //   ALUsignals
  //   isBeq
  //   isBgt
  //   isUBranch
  //   CONTROL
  //   UNIT
  //   isLd
  //   isSt
  //   isCall
  //   isBeq
  //   isWb
  //   isLd
  //   isSt
  //   M5
  //   isWb
  //   address
  //   data
  //   isBgt
  //   isUBranch
  //   isCall
  //   isBeq
  //   isBgt
  //   isWb
  //   isLd
  //   isUBranch
  //   isCall
  //   isSt
  //   to EX
  //   isCall
  //   isLd
  //   Pipieline
endmodule

module Control_Unit (
  input  I_bit,
  input  [4:0] opcode,
  output isSt,
  output isLd,
  output isBeq,
  output isBgt,
  output isRet,
  output isImmediate,
  output isWb,
  output isUbranch,
  output isCall,
  output [12:0] ALUsignals
);

  wire and_6_out, and_7_out, and_8_out, and_9_out, and_10_out, and_12_out, and_13_out, nand_1_out;

  nand nand_1 (nand_1_out, opcode[0], opcode[1]);
  and and_1 (isSt, opcode[0], opcode[1], opcode[2], opcode[3], ~opcode[4]);  // AND_Gate
  and and_2 (isLd, ~opcode[0], opcode[1], opcode[2], opcode[3], ~opcode[4]);  // AND_Gate
  and and_3 (isBeq, ~opcode[0], ~opcode[1], ~opcode[2], ~opcode[3], opcode[4]);  // AND_Gate
  and and_4 (isBgt, opcode[0], ~opcode[1], ~opcode[2], ~opcode[3], opcode[4]);  // AND_Gate
  and and_5 (isRet, ~opcode[0], ~opcode[1], opcode[2], ~opcode[3], opcode[4]);  // AND_Gate
  and and_6 (and_6_out, opcode[0], ~opcode[1], opcode[2], ~opcode[4]);  // AND_Gate
  and and_7 (and_7_out, opcode[0], opcode[2], opcode[3], ~opcode[4]);  // AND_Gate
  and and_8 (and_8_out, opcode[4], nand_1_out);
  and and_9 (and_9_out, opcode[1], ~opcode[2], ~opcode[3], opcode[4]);  // AND_Gate
  and and_10 (and_10_out, ~opcode[0], ~opcode[1], opcode[2], ~opcode[3], opcode[4]);  // AND_Gate
  and and_11 (isCall, opcode[0], opcode[1], ~opcode[2], ~opcode[3], opcode[4]);  // AND_Gate
  and and_12 (and_12_out, ~opcode[0], ~opcode[1], ~opcode[2], ~opcode[3], ~opcode[4]);  // AND_Gate
  and and_13 (and_13_out, opcode[1], opcode[2], opcode[3], ~opcode[4]);  // AND_Gate
  and isSub (ALUsignals[2], opcode[0], ~opcode[1], ~opcode[2], ~opcode[3], ~opcode[4]);  // AND_Gate
  and isCmp (ALUsignals[0], opcode[0], ~opcode[1], opcode[2], ~opcode[3], ~opcode[4]);  // AND_Gate
  and isMul (ALUsignals[3], ~opcode[0], opcode[1], ~opcode[2], ~opcode[3], ~opcode[4]);  // AND_Gate
  and isDiv (ALUsignals[4], opcode[0], opcode[1], ~opcode[2], ~opcode[3], ~opcode[4]);  // AND_Gate
  and isMod (ALUsignals[5], ~opcode[0], ~opcode[1], opcode[2], ~opcode[3], ~opcode[4]);  // AND_Gate
  and isLsl (ALUsignals[7], ~opcode[0], opcode[1], ~opcode[2], opcode[3], ~opcode[4]);  // AND_Gate
  and isLsr (ALUsignals[8], opcode[0], opcode[1], ~opcode[2], opcode[3], ~opcode[4]);  // AND_Gate
  and isAsr (ALUsignals[9], ~opcode[0], ~opcode[1], opcode[2], opcode[3], ~opcode[4]);  // AND_Gate
  and isOr (ALUsignals[12], opcode[0], opcode[1], opcode[2], ~opcode[3], ~opcode[4]);  // AND_Gate
  and isAnd (ALUsignals[11], ~opcode[0], opcode[1], opcode[2], ~opcode[3], ~opcode[4]);  // AND_Gate
  and isNot (ALUsignals[10], ~opcode[0], ~opcode[1], ~opcode[2], opcode[3], ~opcode[4]);  // AND_Gate
  and isMov (ALUsignals[6], opcode[0], ~opcode[1], ~opcode[2], opcode[3], ~opcode[4]);  // AND_Gate
  or or_1 (isUbranch, and_9_out, and_10_out);
  or isAdd (ALUsignals[1], and_12_out, and_13_out);
  nor nor_1 (isWb, and_6_out, and_7_out, and_8_out);

  assign isImmediate = I_bit;

  // Notes on the sheet:
  //   op1
  //   op2
  //   op3
  //   op4
  //   op5
endmodule

module Register_File (
  input  Clock,
  input  Reset,
  input  [31:0] WriteD,
  input  [3:0] ReadA1,
  input  WriteE,
  input  [3:0] WriteA,
  input  [3:0] ReadA2,
  input  [3:0] DisplayA,
  output [31:0] ReadD1,
  output [31:0] ReadD2,
  output [31:0] DisplayD
);

  wire demultiplexer_1_out0, demultiplexer_1_out1, demultiplexer_1_out2, demultiplexer_1_out3,
       demultiplexer_1_out4, demultiplexer_1_out5, demultiplexer_1_out6, demultiplexer_1_out7,
       demultiplexer_1_out8, demultiplexer_1_out9, demultiplexer_1_out10, demultiplexer_1_out11,
       demultiplexer_1_out12, demultiplexer_1_out13, demultiplexer_1_out14, demultiplexer_1_out15,
       multiplexer_2_out, or_1_out, or_2_out;
  wire [31:0] multiplexer_1_out, r0_q, r1_q, r2_q, r3_q, r4_q, r5_q, r6_q, r7_q, r8_q, r9_q, r10_q, r11_q,
       r12_q, r13_q, r14_q, r15_q;

  Demultiplexer #(.select(4), .disabled(0), .enable("false")) demultiplexer_1 (
    .out0(demultiplexer_1_out0), .out1(demultiplexer_1_out1), .out2(demultiplexer_1_out2),
    .out3(demultiplexer_1_out3), .out4(demultiplexer_1_out4), .out5(demultiplexer_1_out5),
    .out6(demultiplexer_1_out6), .out7(demultiplexer_1_out7), .out8(demultiplexer_1_out8),
    .out9(demultiplexer_1_out9), .out10(demultiplexer_1_out10), .out11(demultiplexer_1_out11),
    .out12(demultiplexer_1_out12), .out13(demultiplexer_1_out13), .out14(demultiplexer_1_out14),
    .out15(demultiplexer_1_out15), .in(WriteE), .sel(WriteA));
  Multiplexer #(.width(32), .enable("false")) multiplexer_1 (
    .in0(WriteD), .in1(32'h3fffffc), .out(multiplexer_1_out), .sel(Reset));
  or or_1 (or_1_out, demultiplexer_1_out14, Reset);
  or or_2 (or_2_out, Clock, Reset);
  Multiplexer #(.enable("false")) multiplexer_2 (.in0(or_2_out), .out(multiplexer_2_out), .sel(1'b0));  // open: in1
  Register #(.width(32)) r0 (.D(WriteD), .en(demultiplexer_1_out0), .Q(r0_q), .clk(Clock), .clr(Reset));
  Register #(.width(32)) r1 (.D(WriteD), .en(demultiplexer_1_out1), .Q(r1_q), .clk(Clock), .clr(Reset));
  Register #(.width(32)) r2 (.D(WriteD), .en(demultiplexer_1_out2), .Q(r2_q), .clk(Clock), .clr(Reset));
  Register #(.width(32)) r3 (.D(WriteD), .en(demultiplexer_1_out3), .Q(r3_q), .clk(Clock), .clr(Reset));
  Register #(.width(32)) r4 (.D(WriteD), .en(demultiplexer_1_out4), .Q(r4_q), .clk(Clock), .clr(Reset));
  Register #(.width(32)) r5 (.D(WriteD), .en(demultiplexer_1_out5), .Q(r5_q), .clk(Clock), .clr(Reset));
  Register #(.width(32)) r6 (.D(WriteD), .en(demultiplexer_1_out6), .Q(r6_q), .clk(Clock), .clr(Reset));
  Register #(.width(32)) r7 (.D(WriteD), .en(demultiplexer_1_out7), .Q(r7_q), .clk(Clock), .clr(Reset));
  Register #(.width(32)) r8 (.D(WriteD), .en(demultiplexer_1_out8), .Q(r8_q), .clk(Clock), .clr(Reset));
  Register #(.width(32)) r9 (.D(WriteD), .en(demultiplexer_1_out9), .Q(r9_q), .clk(Clock), .clr(Reset));
  Register #(.width(32)) r10 (.D(WriteD), .en(demultiplexer_1_out10), .Q(r10_q), .clk(Clock), .clr(Reset));
  Register #(.width(32)) r11 (.D(WriteD), .en(demultiplexer_1_out11), .Q(r11_q), .clk(Clock), .clr(Reset));
  Register #(.width(32)) r12 (.D(WriteD), .en(demultiplexer_1_out12), .Q(r12_q), .clk(Clock), .clr(Reset));
  Register #(.width(32)) r13 (.D(WriteD), .en(demultiplexer_1_out13), .Q(r13_q), .clk(Clock), .clr(Reset));
  Register #(.width(32)) r14 (.D(multiplexer_1_out), .en(or_1_out), .Q(r14_q), .clk(multiplexer_2_out));  // open: clr
  Register #(.width(32)) r15 (.D(WriteD), .en(demultiplexer_1_out15), .Q(r15_q), .clk(Clock), .clr(Reset));
  Multiplexer #(.select(4), .width(32), .disabled(0), .enable("false")) multiplexer_3 (
    .in0(r0_q), .in1(r1_q), .in2(r2_q), .in3(r3_q), .in4(r4_q), .in5(r5_q), .in6(r6_q), .in7(r7_q),
    .in8(r8_q), .in9(r9_q), .in10(r10_q), .in11(r11_q), .in12(r12_q), .in13(r13_q), .in14(r14_q),
    .in15(r15_q), .out(ReadD1), .sel(ReadA1));
  Multiplexer #(.select(4), .width(32), .disabled(0), .enable("false")) multiplexer_4 (
    .in0(r0_q), .in1(r1_q), .in2(r2_q), .in3(r3_q), .in4(r4_q), .in5(r5_q), .in6(r6_q), .in7(r7_q),
    .in8(r8_q), .in9(r9_q), .in10(r10_q), .in11(r11_q), .in12(r12_q), .in13(r13_q), .in14(r14_q),
    .in15(r15_q), .out(ReadD2), .sel(ReadA2));
  Multiplexer #(.select(4), .width(32), .disabled(0), .enable("false")) multiplexer_5 (
    .in0(r0_q), .in1(r1_q), .in2(r2_q), .in3(r3_q), .in4(r4_q), .in5(r5_q), .in6(r6_q), .in7(r7_q),
    .in8(r8_q), .in9(r9_q), .in10(r10_q), .in11(r11_q), .in12(r12_q), .in13(r13_q), .in14(r14_q),
    .in15(r15_q), .out(DisplayD), .sel(DisplayA));
endmodule

module ALU (
  input  [31:0] A,
  input  [31:0] B,
  input  [12:0] ALUsignals,
  output [31:0] aluResult,
  output is,
  output is_2
);

  wire [31:0] adder_1_out, and_1_out, divider_1_out, divider_1_rem, multiplier_1_out, not_1_out, or_1_out,
       shifter_1_out, shifter_2_out, shifter_3_out, subtractor_1_out;

  Adder #(.width(32)) adder_1 (.a(A), .b(B), .out(adder_1_out));  // open: cin, cout
  Subtractor #(.width(32)) subtractor_1 (.a(A), .b(B), .out(subtractor_1_out));  // open: bin, bout
  Multiplier #(.width(32)) multiplier_1 (.a(A), .b(B), .out(multiplier_1_out));  // open: cin, cout
  Divider #(.width(32)) divider_1 (.a(A), .b(B), .out(divider_1_out), .rem(divider_1_rem));  // open: upper
  Comparator #(.width(32)) comparator_1 (.a(A), .b(B), .gt(is), .eq(is_2));  // open: lt
  Shifter #(.width(32)) shifter_1 (.in(A), .\dist (B[4:0]), .out(shifter_1_out));
  Shifter #(.width(32), .shift("lr")) shifter_2 (.in(A), .\dist (B[4:0]), .out(shifter_2_out));
  Shifter #(.width(32), .shift("ar")) shifter_3 (.in(A), .\dist (B[4:0]), .out(shifter_3_out));
  assign not_1_out = ~B;  // NOT_Gate not_1, 32 bits wide
  assign and_1_out = A & B;  // AND_Gate and_1, 32 bits wide
  assign or_1_out = A | B;  // OR_Gate or_1, 32 bits wide
  assign aluResult = ALUsignals[1] ? adder_1_out : 32'bz;  // Controlled_Buffer controlled_buffer_1
  assign aluResult = ALUsignals[2] ? subtractor_1_out : 32'bz;  // Controlled_Buffer controlled_buffer_2
  assign aluResult = ALUsignals[3] ? multiplier_1_out : 32'bz;  // Controlled_Buffer controlled_buffer_3
  assign aluResult = ALUsignals[4] ? divider_1_out : 32'bz;  // Controlled_Buffer controlled_buffer_4
  assign aluResult = ALUsignals[5] ? divider_1_rem : 32'bz;  // Controlled_Buffer controlled_buffer_5
  assign aluResult = ALUsignals[6] ? B : 32'bz;  // Controlled_Buffer controlled_buffer_6
  assign aluResult = ALUsignals[7] ? shifter_1_out : 32'bz;  // Controlled_Buffer controlled_buffer_7
  assign aluResult = ALUsignals[8] ? shifter_2_out : 32'bz;  // Controlled_Buffer controlled_buffer_8
  assign aluResult = ALUsignals[9] ? shifter_3_out : 32'bz;  // Controlled_Buffer controlled_buffer_9
  assign aluResult = ALUsignals[10] ? not_1_out : 32'bz;  // Controlled_Buffer controlled_buffer_10
  assign aluResult = ALUsignals[11] ? and_1_out : 32'bz;  // Controlled_Buffer controlled_buffer_11
  assign aluResult = ALUsignals[12] ? or_1_out : 32'bz;  // Controlled_Buffer controlled_buffer_12

  // Notes on the sheet:
  //   add
  //   sub
  //   mul
  //   div
  //   cmp
  //   lsr
  //   mod
  //   lsl
  //   asr
endmodule

module Flags (
  input  isCmp,
  input  is,
  input  is_2,
  output flags_GT,
  output flags_E
);

  D_Flip_Flop #(.trigger("high")) d_ff_1 (.clk(isCmp), .D(is), .Q(flags_GT));  // open: Qn, preset, en, reset
  D_Flip_Flop #(.trigger("high")) d_ff_2 (.clk(isCmp), .D(is_2), .Q(flags_E));  // open: Qn, preset, en, reset
endmodule

module Branch_Unit (
  input  isUBranch,
  input  isBeq,
  input  flags_E,
  input  isBgt,
  input  flags_GT,
  output isBranchTaken
);

  wire and_1_out, and_2_out;

  and and_1 (and_1_out, isBeq, flags_E);
  and and_2 (and_2_out, isBgt, flags_GT);
  or or_1 (isBranchTaken, isUBranch, and_1_out, and_2_out);
endmodule

module Memory_Unit (
  input  [31:0] MAR,
  input  isLd,
  input  [31:0] MDR,
  input  isSt,
  input  Clock,
  input  Reset,
  output [31:0] ldResult
);

  RAM #(.addrWidth(24), .dataWidth(32), .bus("separate")) ram_1 (
    .addr(MAR[25:2]), .din(MDR), .data(ldResult), .str(isSt), .clk(Clock), .ld(isLd), .clr(Reset));  // open: sel
endmodule

module Calculate_Immediate (
  input  [17:0] imm,
  output [31:0] immx
);

  wire [31:0] bit_extender_1_out, bit_extender_2_out, shifter_1_out;

  assign bit_extender_1_out = {{16{1'b0}}, imm[15:0]};  // Bit_Extender bit_extender_1
  assign bit_extender_2_out = {{16{imm[15]}}, imm[15:0]};  // Bit_Extender bit_extender_2
  Shifter #(.width(32)) shifter_1 (.in(bit_extender_1_out), .\dist (5'b10000), .out(shifter_1_out));
  Multiplexer #(.select(2), .width(32), .enable("false")) multiplexer_1 (
    .in0(bit_extender_2_out), .in1(bit_extender_1_out), .in2(shifter_1_out), .out(immx), .sel(imm[17:16]));  // open: in3

  // Notes on the sheet:
  //   modifier bits
  //   high
  //   default
  //   unsigned
endmodule

module IF_OF_STAGE (
  input  [31:0] in_1,
  input  [31:0] in_2,
  input  in_3,
  output [31:0] out_4,
  output [31:0] out_5
);

  Register #(.width(32)) PC (.D(in_1), .Q(out_4), .clk(in_3));  // open: en, clr
  Register #(.width(32)) INSTRUCTION (.D(in_2), .Q(out_5), .clk(in_3));  // open: en, clr
endmodule

module DataLock (
  input  [31:0] Inst1,
  input  [31:0] Inst2_Load,
  output isDataLock
);

  wire and_1_out, and_2_out, and_3_out, and_4_out, checkSource_hassrc1, checkSource_hassrc2, or_1_out;
  wire [3:0] xnor_1_out, xnor_2_out;

  DetectSrc checkSource (
    .A(Inst1[31]), .B(Inst1[30]), .C(Inst1[29]), .D(Inst1[28]), .E(Inst1[27]), .hasSrc1(checkSource_hassrc1),
    .hasSrc2(checkSource_hassrc2));
  and and_1 (and_1_out, ~Inst2_Load[31], Inst2_Load[30], Inst2_Load[29], Inst2_Load[28], ~Inst2_Load[27]);  // AND_Gate
  and and_2 (and_2_out, checkSource_hassrc2, ~Inst1[26]);  // AND_Gate
  assign xnor_1_out = ~(Inst1[21:18] ^ Inst2_Load[25:22]);  // XNOR_Gate xnor_1, 4 bits wide
  assign xnor_2_out = ~(Inst2_Load[25:22] ^ Inst1[17:14]);  // XNOR_Gate xnor_2, 4 bits wide
  and and_3 (and_3_out, checkSource_hassrc1, xnor_1_out[0], xnor_1_out[1], xnor_1_out[2], xnor_1_out[3]);
  and and_4 (and_4_out, and_2_out, xnor_2_out[0], xnor_2_out[1], xnor_2_out[2], xnor_2_out[3]);
  or or_1 (or_1_out, and_3_out, and_4_out);
  and and_5 (isDataLock, and_1_out, or_1_out);

  // Notes on the sheet:
  //   Load Opcode
  //   Comparator
endmodule

module DetectSrc (
  input  A,
  input  B,
  input  C,
  input  D,
  input  E,
  output hasSrc1,
  output hasSrc2
);

  wire and_1_out, and_2_out, and_3_out, and_4_out, and_5_out, and_6_out, and_7_out, and_8_out, not_1_out,
       not_2_out, not_3_out, not_4_out, not_5_out, not_6_out, not_7_out, not_8_out, not_9_out, not_10_out,
       not_11_out, not_12_out, not_13_out, not_14_out, not_15_out;

  not not_1 (not_1_out, A);
  not not_2 (not_2_out, B);
  not not_3 (not_3_out, B);
  not not_4 (not_4_out, D);
  not not_5 (not_5_out, A);
  not not_6 (not_6_out, E);
  not not_7 (not_7_out, A);
  not not_8 (not_8_out, B);
  not not_9 (not_9_out, A);
  not not_10 (not_10_out, C);
  not not_11 (not_11_out, A);
  not not_12 (not_12_out, D);
  not not_13 (not_13_out, E);
  not not_14 (not_14_out, C);
  not not_15 (not_15_out, D);
  and and_1 (and_1_out, not_1_out, not_2_out);
  and and_2 (and_2_out, not_3_out, not_4_out);
  and and_3 (and_3_out, not_5_out, D);
  and and_4 (and_4_out, C, not_6_out);
  and and_5 (and_5_out, not_7_out, not_8_out);
  and and_6 (and_6_out, not_9_out, not_10_out);
  and and_7 (and_7_out, not_11_out, not_12_out, not_13_out);
  and and_8 (and_8_out, not_14_out, not_15_out);
  or or_1 (hasSrc1, and_1_out, and_2_out, and_3_out, and_4_out);
  or or_2 (hasSrc2, and_5_out, and_6_out, and_7_out, and_8_out);
endmodule

module Src1_Conflict_Aopcode (
  input  [4:0] in_1,
  output X
);

  wire and_1_out, and_2_out, and_3_out, and_4_out, and_5_out, not_1_out, not_2_out, not_3_out, not_4_out,
       not_5_out;

  not not_1 (not_1_out, in_1[4]);
  not not_2 (not_2_out, in_1[3]);
  not not_3 (not_3_out, in_1[4]);
  not not_4 (not_4_out, in_1[3]);
  not not_5 (not_5_out, in_1[0]);
  and and_1 (and_1_out, not_1_out, not_2_out);
  and and_2 (and_2_out, not_3_out, in_1[1]);
  and and_3 (and_3_out, not_4_out, in_1[2]);
  and and_4 (and_4_out, in_1[2], not_5_out);
  and and_5 (and_5_out, in_1[4], in_1[3]);
  or or_1 (X, and_1_out, and_2_out, and_3_out, and_4_out, and_5_out);
endmodule

module Src2_Conflict_Aopcode (
  input  [4:0] in_1,
  output A1
);

  wire and_1_out, and_2_out, and_3_out, and_4_out, and_5_out, not_1_out, not_2_out, not_3_out, not_4_out,
       not_5_out, not_6_out;

  not not_1 (not_1_out, in_1[4]);
  not not_2 (not_2_out, in_1[3]);
  not not_3 (not_3_out, in_1[4]);
  not not_4 (not_4_out, in_1[0]);
  not not_5 (not_5_out, in_1[4]);
  not not_6 (not_6_out, in_1[2]);
  and and_1 (and_1_out, not_1_out, not_2_out);
  and and_2 (and_2_out, not_3_out, not_4_out);
  and and_3 (and_3_out, not_5_out, in_1[1]);
  and and_4 (and_4_out, in_1[3], not_6_out);
  and and_5 (and_5_out, in_1[4], in_1[2]);
  or or_1 (A1, and_1_out, and_2_out, and_3_out, and_4_out, and_5_out);
endmodule

module check_Bopcode (
  input  [4:0] in_1,
  output X
);

  wire and_1_out, and_2_out, and_3_out, and_4_out, and_5_out, and_6_out, not_1_out, not_2_out, not_3_out,
       not_4_out, not_5_out, not_6_out;

  not not_1 (not_1_out, in_1[4]);
  not not_2 (not_2_out, in_1[2]);
  not not_3 (not_3_out, in_1[4]);
  not not_4 (not_4_out, in_1[0]);
  not not_5 (not_5_out, in_1[3]);
  not not_6 (not_6_out, in_1[3]);
  and and_1 (and_1_out, not_1_out, not_2_out);
  and and_2 (and_2_out, not_3_out, not_4_out);
  and and_3 (and_3_out, not_5_out, in_1[1], in_1[0]);
  and and_4 (and_4_out, not_6_out, in_1[2], in_1[1]);
  and and_5 (and_5_out, in_1[4], in_1[2], in_1[0]);
  and and_6 (and_6_out, in_1[4], in_1[3]);
  or or_1 (X, and_1_out, and_2_out, and_3_out, and_4_out, and_5_out, and_6_out);
endmodule

module Conflict_Src1 (
  input  [31:0] A,
  input  [31:0] B,
  input  [3:0] ra,
  output out_4
);

  wire check_A_opcode_x, check_B_opcode_x, check_Call_iscall, check_ret_x;
  wire [3:0] multiplexer_1_out, multiplexer_2_out, xnor_1_out;

  Src1_Conflict_Aopcode check_A_opcode (.in_1(A[31:27]), .X(check_A_opcode_x));
  checkRet check_ret (.in_1(A[31:27]), .X(check_ret_x));
  check_Bopcode check_B_opcode (.in_1(B[31:27]), .X(check_B_opcode_x));
  checkCall check_Call (.opcode(B[31:27]), .isCall(check_Call_iscall));
  Multiplexer #(.width(4)) multiplexer_1 (
    .in0(A[21:18]), .in1(ra), .out(multiplexer_1_out), .sel(check_ret_x));  // open: en
  Multiplexer #(.width(4)) multiplexer_2 (
    .in0(B[25:22]), .in1(ra), .out(multiplexer_2_out), .sel(check_Call_iscall));  // open: en
  assign xnor_1_out = ~(multiplexer_1_out ^ multiplexer_2_out);  // XNOR_Gate xnor_1, 4 bits wide
  and and_1 (out_4, check_A_opcode_x, check_B_opcode_x, xnor_1_out[0], xnor_1_out[1], xnor_1_out[2], xnor_1_out[3]);

  // Notes on the sheet:
  //   opcode
  //   rs1
  //   opcode
  //   rd
  //   src1
  //   dest
endmodule

module Conflict_Src2 (
  input  [31:0] A,
  input  [31:0] B,
  input  [3:0] ra,
  output out_4
);

  wire and_1_out, check_A_opcode_a1, check_B_opcode_x, check_Call_iscall, check_Store_isstore, not_1_out,
       or_1_out;
  wire [3:0] multiplexer_1_out, multiplexer_2_out, xnor_1_out;

  Src2_Conflict_Aopcode check_A_opcode (.in_1(A[31:27]), .A1(check_A_opcode_a1));
  checkStore check_Store (.opcode(A[31:27]), .isStore(check_Store_isstore));
  not not_1 (not_1_out, A[26]);
  check_Bopcode check_B_opcode (.in_1(B[31:27]), .X(check_B_opcode_x));
  checkCall check_Call (.opcode(B[31:27]), .isCall(check_Call_iscall));
  or or_1 (or_1_out, not_1_out, check_Store_isstore);
  Multiplexer #(.width(4)) multiplexer_1 (
    .in0(A[17:14]), .in1(A[25:22]), .out(multiplexer_1_out), .sel(check_Store_isstore));  // open: en
  Multiplexer #(.width(4)) multiplexer_2 (
    .in0(B[25:22]), .in1(ra), .out(multiplexer_2_out), .sel(check_Call_iscall));  // open: en
  and and_1 (and_1_out, check_A_opcode_a1, or_1_out, check_B_opcode_x);
  assign xnor_1_out = ~(multiplexer_1_out ^ multiplexer_2_out);  // XNOR_Gate xnor_1, 4 bits wide
  and and_2 (out_4, and_1_out, xnor_1_out[0], xnor_1_out[1], xnor_1_out[2], xnor_1_out[3]);

  // Notes on the sheet:
  //   src2
  //   dest
endmodule

module checkRet (
  input  [4:0] in_1,
  output X
);

  and and_1 (X, ~in_1[0], ~in_1[1], in_1[2], ~in_1[3], in_1[4]);  // AND_Gate
endmodule

module checkCall (
  input  [4:0] opcode,
  output isCall
);

  and and_1 (isCall, opcode[0], opcode[1], ~opcode[2], ~opcode[3], opcode[4]);  // AND_Gate
endmodule

module checkStore (
  input  [4:0] opcode,
  output isStore
);

  and and_1 (isStore, opcode[0], opcode[1], opcode[2], opcode[3], ~opcode[4]);  // AND_Gate
endmodule

module checkLoad (
  input  [4:0] opcode,
  output isLoad
);

  and and_1 (isLoad, ~opcode[0], opcode[1], opcode[2], opcode[3], ~opcode[4]);  // AND_Gate
endmodule

module temp (
  input  [31:0] A,
  input  [31:0] B,
  input  [3:0] ra,
  output out_4
);

  wire and_1_out, check_A_opcode_a1, check_B_opcode_x, checkcall_1_iscall, checkstore_1_isstore, not_1_out,
       or_1_out;
  wire [3:0] multiplexer_1_out, multiplexer_2_out, xnor_1_out;

  Multiplexer #(.width(4)) multiplexer_1 (
    .in0(A[17:14]), .in1(A[25:22]), .out(multiplexer_1_out), .sel(checkstore_1_isstore));  // open: en
  not not_1 (not_1_out, A[26]);
  checkStore checkstore_1 (.opcode(A[31:27]), .isStore(checkstore_1_isstore));
  Multiplexer #(.width(4)) multiplexer_2 (
    .in0(B[25:22]), .in1(ra), .out(multiplexer_2_out), .sel(checkcall_1_iscall));  // open: en
  Src2_Conflict_Aopcode check_A_opcode (.in_1(A[31:27]), .A1(check_A_opcode_a1));
  or or_1 (or_1_out, not_1_out, checkstore_1_isstore);
  check_Bopcode check_B_opcode (.in_1(B[31:27]), .X(check_B_opcode_x));
  checkCall checkcall_1 (.opcode(B[31:27]), .isCall(checkcall_1_iscall));
  and and_1 (and_1_out, check_A_opcode_a1, or_1_out, check_B_opcode_x);
  assign xnor_1_out = ~(multiplexer_1_out ^ multiplexer_2_out);  // XNOR_Gate xnor_1, 4 bits wide
  and and_2 (out_4, and_1_out, xnor_1_out[0], xnor_1_out[1], xnor_1_out[2], xnor_1_out[3]);

  // Notes on the sheet:
  //   src2
  //   dest
endmodule
